# Fritzing sketch conexiones (saved by Fritzing 0.9.6b)

parts:
  DHT11_1 = DHT11 module
  Raspberry_Pi1 = Raspberry Pi 2

nets:
  VCC: DHT11_1.VCC, Raspberry_Pi1.5V
  GND: DHT11_1.GND, Raspberry_Pi1.GND
  N1: DHT11_1.DATA, Raspberry_Pi1.GPIO4

custom parts:
  DHT11 module: https://cdn-learn.adafruit.com/downloads/pdf/dht.pdf DHT11 black pcb module reference by:https://github.com/adafruit/Fritzing-Library/blob/master/parts/DHT11%20Humitidy%20and%20Temperature%20Sensor.fzpz
