# Fritzing sketch conexiones (saved by Fritzing 0.9.6b)

parts:
  e-radionica_com1 = LM393 LDR breakout [part_number=100027]
  Raspberry_Pi1 = Raspberry Pi 2

nets:
  VCC: e-radionica_com1.VCC, Raspberry_Pi1.3v3
  GND: e-radionica_com1.GND, Raspberry_Pi1.GND
  N1: e-radionica_com1.DO, Raspberry_Pi1.GPIO14
