# Fritzing sketch conexines (saved by Fritzing 0.9.6b)

parts:
  Part1 = RFID-RC522-v3
  Raspberry_Pi1 = Raspberry Pi 2

nets:
  N1: Part1.SDA, Raspberry_Pi1.GPIO8
  N2: Part1.SCK, Raspberry_Pi1.GPIO11
  N3: Part1.MOSI, Raspberry_Pi1.GPIO10
  N4: Part1.MISO, Raspberry_Pi1.GPIO9
  GND: Part1.GND, Raspberry_Pi1.GND
  N5: Part1.RST, Raspberry_Pi1.GPIO25
  3.3V: Part1.3.3V, Raspberry_Pi1.3v3

custom parts:
  RFID-RC522-v3: A simple China made RFID-RC522 Reader (6x4 cm); do check the pin labels, as this is a MFRC522 based clone.
