# Fritzing sketch conexiones (saved by Fritzing 0.9.6b)

parts:
  Raspberry_Pi1 = Raspberry Pi 2
  U1 = 2-Channel 5v Relay Shield [package=relay-2ch5v10a]

nets:
  N1: Raspberry_Pi1.GPIO18, U1.IN1
  GND: Raspberry_Pi1.GND, U1.GND
  5V: Raspberry_Pi1.5V, U1.VCC

custom parts:
  2-Channel 5v Relay Shield: 2 Channel 5v Relay Shield w. 2x SPD-06VDC-SD-C
