# Fritzing sketch PanTilt-AlimentacionExterna (saved by Fritzing 0.9.3b)
breadboards: 1

parts:
  Raspberry_Pi1 = Raspberry Pi 2
  TILT_SERVO = Basic Servo
  PAN_SERVO = Basic Servo

nets:
  GND: Raspberry_Pi1.GND, TILT_SERVO.gnd, PAN_SERVO.gnd
  VCC: TILT_SERVO.vcc, PAN_SERVO.vcc

notes:
  GND
  5V
